# Fritzing sketch CANbusv2 (saved by Fritzing 0.9.3b)
breadboards: 1

parts:
  Raspberry_Pi_2 = Raspberry Pi 3 [part_number=RPI-3-V1.2]  # not connected
  Part1 = SeeedStudio Can-Bus Shield
  Part2 = Arduino Uno (Rev3) - ICSP
  Part3 = Arduino Uno (Rev3) - ICSP
  Part4 = SeeedStudio Can-Bus Shield
  U1 = POT [package=pot_alpha_rv16af-20]
  J2 = Basic Servo

nets:
  5V: Part1.5V, Part2.5V, U1.E
  N1: Part1.GND, U1.A
  N2: Part1.CANH, Part4.CANH
  N3: Part1.CANL, Part4.CANL
  N4: Part2.A0, U1.S
  5V_2: Part3.5V, Part4.5V, J2.vcc
  N5: Part3.D9_PWM, J2.pulse
  GND: Part4.GND, J2.gnd

custom parts:
  SeeedStudio Can-Bus Shield: This CAN-BUS Shield adopts MCP2515 CAN Bus controller with SPI interface and MCP2551 CAN transceiver to give your Arduino/Seeeduino CAN-BUS capibility. With an OBD-II converter cable added on and the OBD-II library imported, you are ready to build an onboard diagnostic device or data logger. Features Implements CAN V2.0B at up to 1 Mb/s SPI Interface up to 10 MHz Standard (11 bit) and extended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
